// Logisim project InstDecoder.circ as structural Verilog: 1 circuit, main circuit InstructionDecoder
module InstructionDecoder (
  input  D0,
  input  D1,
  input  D2,
  input  D3,
  input  CLK,
  output INST,
  output NUM,
  output D4,
  output D5,
  output D6,
  output D7,
  output NOP_Out,
  output ADD_Out,
  output SUB_Out,
  output WT1_Out,
  output WT2_Out,
  output WTX_Out,
  output WTY_Out,
  output WTZ_Out,
  output ZTR_Out,
  output RTZ_Out,
  output PC1_Out,
  output PC2_Out,
  output JMP_Out,
  output RTX_Out,
  output RTY_Out,
  output USC_Out
);

  wire [3:0] INSTRUCTION_q, not_2_out;

  Counter #(.max('h1), .width(1)) counter_1 (.clk(CLK), .carry(NUM));  // open: clr, load, up, count, D, Q
  and NOP (NOP_Out, not_2_out[0], not_2_out[1], not_2_out[2], not_2_out[3]);
  and ADD (ADD_Out, INSTRUCTION_q[0], not_2_out[1], not_2_out[2], not_2_out[3]);
  and SUB (SUB_Out, not_2_out[0], INSTRUCTION_q[1], not_2_out[2], not_2_out[3]);
  and WT1 (WT1_Out, INSTRUCTION_q[0], INSTRUCTION_q[1], not_2_out[2], not_2_out[3]);
  and WT2 (WT2_Out, not_2_out[0], not_2_out[1], INSTRUCTION_q[2], not_2_out[3]);
  and WTX (WTX_Out, INSTRUCTION_q[0], not_2_out[1], INSTRUCTION_q[2], not_2_out[3]);
  and WTY (WTY_Out, not_2_out[0], INSTRUCTION_q[1], INSTRUCTION_q[2], not_2_out[3]);
  and WTZ (WTZ_Out, INSTRUCTION_q[0], INSTRUCTION_q[1], INSTRUCTION_q[2], not_2_out[3]);
  and ZTR (ZTR_Out, not_2_out[0], not_2_out[1], not_2_out[2], INSTRUCTION_q[3]);
  and RTZ (RTZ_Out, INSTRUCTION_q[0], not_2_out[1], not_2_out[2], INSTRUCTION_q[3]);
  and PC1 (PC1_Out, not_2_out[0], INSTRUCTION_q[1], not_2_out[2], INSTRUCTION_q[3]);
  and PC2 (PC2_Out, INSTRUCTION_q[0], INSTRUCTION_q[1], not_2_out[2], INSTRUCTION_q[3]);
  and JMP (JMP_Out, not_2_out[0], not_2_out[1], INSTRUCTION_q[2], INSTRUCTION_q[3]);
  and RTX (RTX_Out, INSTRUCTION_q[0], not_2_out[1], INSTRUCTION_q[2], INSTRUCTION_q[3]);
  and RTY (RTY_Out, not_2_out[0], INSTRUCTION_q[1], INSTRUCTION_q[2], INSTRUCTION_q[3]);
  and USC (USC_Out, INSTRUCTION_q[0], INSTRUCTION_q[1], INSTRUCTION_q[2], INSTRUCTION_q[3]);
  Register #(.width(4)) INSTRUCTION (.D({D3, D2, D1, D0}), .en(INST), .clk(INST), .Q(INSTRUCTION_q));  // open: clr
  not not_1 (INST, NUM);
  Register #(.width(4)) NUMBER (.D({D3, D2, D1, D0}), .en(NUM), .clk(NUM), .Q({D7, D6, D5, D4}));  // open: clr
  assign not_2_out = ~INSTRUCTION_q;  // NOT_Gate not_2, 4 bits wide
endmodule
