// Logisim project PBPUMk4.circ as structural Verilog: 1 circuit, main circuit main
module main (
);

  wire adder_1_cout, Carry_q, CLK_out, counter_2_carry, CWE_out, decoder_1_out0, decoder_1_out1,
       decoder_1_out2, decoder_1_out3, decoder_1_out4, decoder_1_out5, decoder_1_out6, decoder_1_out7,
       decoder_1_out8, decoder_1_out9, decoder_1_out13, decoder_1_out14, JMP_out, OE_out,
       pull_resistor_1_node, pull_resistor_2_node, pull_resistor_3_node, pull_resistor_6_node,
       pull_resistor_8_node, pull_resistor_12_node, pull_resistor_14_node, subtractor_1_bout;
  wire [3:0] adder_1_out, controlled_buffer_1_out, controlled_buffer_4_out, Loc1_q, Loc2_q, not_1_out, PC1_q,
       PC2_q, ram_1_dout, rom_1_data, subtractor_1_out, X_q, Y_q, Z_q;
  wire [7:0] counter_1_q;
  wire [7:4] rom_1_data_2;

  Clock CLK (.out(CLK_out));
  Register #(.width(4)) PC1 (.D(rom_1_data), .en(pull_resistor_1_node), .clk(CLK_out), .Q(PC1_q));  // open: clr
  Register #(.width(4)) PC2 (.D(rom_1_data), .en(pull_resistor_2_node), .clk(CLK_out), .Q(PC2_q));  // open: clr
  Counter counter_1 (
    .load(JMP_out), .clk(CLK_out), .D({PC2_q, PC1_q}), .Q(counter_1_q));  // open: clr, up, count, carry
  ROM rom_1 (.addr(counter_1_q), .data({rom_1_data_2, rom_1_data}));
  Pull_Resistor pull_resistor_1 (.node(pull_resistor_1_node));
  Pull_Resistor pull_resistor_2 (.node(pull_resistor_2_node));
  and JMP (JMP_out, pull_resistor_3_node, not_1_out[0], not_1_out[1], not_1_out[2], not_1_out[3]);
  assign not_1_out = ~Z_q;  // NOT_Gate not_1, 4 bits wide
  Pull_Resistor pull_resistor_3 (.node(pull_resistor_3_node));
  Decoder #(.select(4), .tristate("true")) decoder_1 (
    .out0(decoder_1_out0), .out1(decoder_1_out1), .out2(decoder_1_out2), .out3(decoder_1_out3),
    .out4(decoder_1_out4), .out5(decoder_1_out5), .out6(decoder_1_out6), .out7(decoder_1_out7),
    .out8(decoder_1_out8), .out9(decoder_1_out9), .out10(pull_resistor_1_node), .out11(pull_resistor_2_node),
    .out12(pull_resistor_3_node), .out13(decoder_1_out13), .out14(decoder_1_out14), .out15(decoder_1_out14),
    .sel(rom_1_data_2));  // open: en
  Pull_Resistor pull_resistor_4 (.node(decoder_1_out0));
  Pull_Resistor pull_resistor_5 (.node(decoder_1_out5));
  Register #(.width(4)) X (.D(rom_1_data), .en(pull_resistor_6_node), .clk(CLK_out), .Q(X_q));  // open: clr
  Pull_Resistor pull_resistor_6 (.node(pull_resistor_6_node));
  assign controlled_buffer_1_out = decoder_1_out6 ? rom_1_data : 4'bz;  // Controlled_Buffer controlled_buffer_1
  or XWE (pull_resistor_6_node, decoder_1_out5, decoder_1_out13);
  Pull_Resistor pull_resistor_7 (.node(decoder_1_out6));
  assign controlled_buffer_1_out = decoder_1_out14 ? ram_1_dout : 4'bz;  // Controlled_Buffer controlled_buffer_2
  or CWE (CWE_out, subtractor_1_bout, adder_1_cout);
  Register #(.width(4)) Y (
    .D(controlled_buffer_1_out), .en(pull_resistor_8_node), .clk(CLK_out), .Q(Y_q));  // open: clr
  Pull_Resistor pull_resistor_8 (.node(pull_resistor_8_node));
  or YWE (pull_resistor_8_node, decoder_1_out6, decoder_1_out14);
  Pull_Resistor pull_resistor_9 (.node(decoder_1_out13));
  Pull_Resistor pull_resistor_10 (.node(decoder_1_out14));
  Register #(.width(1)) Carry (.D(CWE_out), .en(CLK_out), .clk(CLK_out), .Q(Carry_q));  // open: clr
  Adder #(.width(4)) adder_1 (.a(X_q), .b(Y_q), .out(adder_1_out), .cin(pull_resistor_12_node), .cout(adder_1_cout));
  Subtractor #(.width(4)) subtractor_1 (
    .a(X_q), .b(Y_q), .out(subtractor_1_out), .bin(pull_resistor_12_node), .bout(subtractor_1_bout));
  Pull_Resistor pull_resistor_11 (.node(decoder_1_out1));
  Counter #(.max('h1), .width(1)) counter_2 (
    .clk(decoder_1_out14), .D(decoder_1_out14), .carry(counter_2_carry));  // open: clr, load, up, count, Q
  Pull_Resistor pull_resistor_12 (.node(pull_resistor_12_node));
  assign pull_resistor_12_node = counter_2_carry ? Carry_q : 1'bz;  // Controlled_Buffer controlled_buffer_3
  assign controlled_buffer_4_out = decoder_1_out7 ? rom_1_data : 4'bz;  // Controlled_Buffer controlled_buffer_4
  assign controlled_buffer_4_out = decoder_1_out1 ? adder_1_out : 4'bz;  // Controlled_Buffer controlled_buffer_5
  assign controlled_buffer_4_out = decoder_1_out2 ? subtractor_1_out : 4'bz;  // Controlled_Buffer controlled_buffer_6
  Pull_Resistor pull_resistor_13 (.node(decoder_1_out7));
  Pull_Resistor pull_resistor_14 (.node(pull_resistor_14_node));
  Register #(.width(4)) Z (
    .D(controlled_buffer_4_out), .en(pull_resistor_14_node), .clk(CLK_out), .Q(Z_q));  // open: clr
  Pull_Resistor pull_resistor_15 (.node(decoder_1_out2));
  or ZWE (pull_resistor_14_node, decoder_1_out1, decoder_1_out2, decoder_1_out7, decoder_1_out9);
  Pull_Resistor pull_resistor_16 (.node(decoder_1_out9));
  Register #(.width(4)) Loc1 (.D(rom_1_data), .en(decoder_1_out3), .clk(CLK_out), .Q(Loc1_q));  // open: clr
  Pull_Resistor pull_resistor_17 (.node(decoder_1_out3));
  Pull_Resistor pull_resistor_18 (.node(decoder_1_out4));
  assign controlled_buffer_4_out = decoder_1_out9 ? ram_1_dout : 4'bz;  // Controlled_Buffer controlled_buffer_7
  Pull_Resistor pull_resistor_19 (.node(decoder_1_out8));
  Register #(.width(4)) Loc2 (.D(rom_1_data), .en(decoder_1_out4), .clk(CLK_out), .Q(Loc2_q));  // open: clr
  RAM #(.dataWidth(4), .trigger("falling")) ram_1 (
    .addr({Loc1_q, Loc2_q}), .we(decoder_1_out8), .oe(OE_out), .clk(CLK_out), .din(Z_q), .dout(ram_1_dout));
  or OE (OE_out, decoder_1_out9, decoder_1_out13, decoder_1_out14);

  // Notes on the sheet:
  //   contents of rom_1 (hex, n*v repeats v):
  //   61 71 51 e0 10 80 a3 70 c0
endmodule
